// Logisim project Team Assignment 01.circ as structural Verilog: 5 circuits, main circuit main
module main (
  input  in_1,
  input  in_2,
  input  in_3,
  input  in_4,
  output out_5
);

  wire ic7404_1_out_7, ic7404_1_out_8, ic7404_1_out_10, ic7411_1_out_10, ic7411_1_out_11, ic7411_1_out_12,
       ic_74ls32_1_out_9, ic_74ls32_1_out_10;

  IC7404 ic7404_1 (
    .in_1(in_1), .in_2(in_2), .in_4(in_3), .out_7(ic7404_1_out_7), .out_8(ic7404_1_out_8),
    .out_10(ic7404_1_out_10));  // open: in_3, in_5, in_6, out_9, out_11, out_12
  IC7411 ic7411_1 (
    .in_1(ic7404_1_out_8), .in_2(ic7404_1_out_7), .in_3(in_3), .in_4(ic7404_1_out_7), .in_5(in_2),
    .in_6(ic7404_1_out_10), .in_7(in_1), .in_8(ic7404_1_out_8), .in_9(ic7404_1_out_10),
    .out_10(ic7411_1_out_10), .out_11(ic7411_1_out_11), .out_12(ic7411_1_out_12));
  IC_74LS32 ic_74ls32_1 (
    .in_1(ic7411_1_out_10), .in_2(ic7411_1_out_11), .in_3(ic_74ls32_1_out_9), .in_4(ic7411_1_out_12),
    .out_9(ic_74ls32_1_out_9), .out_10(ic_74ls32_1_out_10));  // open: in_5, in_6, in_7, in_8, out_11, out_12
  IC_7408 IC7408 (
    .in_1(ic_74ls32_1_out_10), .in_2(in_4), .out_9(out_5));  // open: in_3, in_4, in_5, in_6, in_7, in_8, out_10, out_11, out_12

  // Notes on the sheet:
  //   A
  //   B
  //   C
  //   D
  //   B
  //   IC7404
  //   C'
  //   B'
  //   A'
  //   A
  //   B'
  //   C'
  //   A'B'C
  //   IC7411
  //   A'BC'
  //   AB'C'
  //   D
  //   IC74LS32
  //   A'B'C'+A'BC'+AB'C'
  //   D(A'B'C'+A'BC'+AB'C')
endmodule

module IC7404 (
  input  in_1,
  input  in_2,
  input  in_3,
  input  in_4,
  input  in_5,
  input  in_6,
  output out_7,
  output out_8,
  output out_9,
  output out_10,
  output out_11,
  output out_12
);

  not not_1 (out_7, in_1);
  not not_2 (out_8, in_2);
  not not_3 (out_9, in_3);
  not not_4 (out_10, in_4);
  not not_5 (out_11, in_5);
  not not_6 (out_12, in_6);
endmodule

module IC7411 (
  input  in_1,
  input  in_2,
  input  in_3,
  input  in_4,
  input  in_5,
  input  in_6,
  input  in_7,
  input  in_8,
  input  in_9,
  output out_10,
  output out_11,
  output out_12
);

  and and_1 (out_10, in_1, in_2, in_3);
  and and_2 (out_11, in_4, in_5, in_6);
  and and_3 (out_12, in_7, in_8, in_9);
endmodule

module IC_74LS32 (
  input  in_1,
  input  in_2,
  input  in_3,
  input  in_4,
  input  in_5,
  input  in_6,
  input  in_7,
  input  in_8,
  output out_9,
  output out_10,
  output out_11,
  output out_12
);

  or or_1 (out_9, in_1, in_2);
  or or_2 (out_10, in_3, in_4);
  or or_3 (out_11, in_5, in_6);
  or or_4 (out_12, in_7, in_8);
endmodule

module IC_7408 (
  input  in_1,
  input  in_2,
  input  in_3,
  input  in_4,
  input  in_5,
  input  in_6,
  input  in_7,
  input  in_8,
  output out_9,
  output out_10,
  output out_11,
  output out_12
);

  and and_1 (out_9, in_1, in_2);
  and and_2 (out_10, in_3, in_4);
  and and_3 (out_11, in_5, in_6);
  and and_4 (out_12, in_7, in_8);
endmodule
