// Logisim project LAB 02 With IC Diagram.circ as structural Verilog: 2 circuits, main circuit main
module main (
  input  A,
  input  B,
  input  C,
  output out_4
);

  wire ic7400_1_out_9, ic7400_1_out_10, ic7400_1_out_11, ic7400_1_out_12, ic7400_2_out_10;

  IC7400 ic7400_1 (
    .in_1(ic7400_1_out_10), .in_2(ic7400_1_out_10), .in_3(C), .in_4(A), .in_5(ic7400_1_out_9),
    .in_6(ic7400_1_out_9), .in_7(C), .in_8(C), .out_9(ic7400_1_out_9), .out_10(ic7400_1_out_10),
    .out_11(ic7400_1_out_11), .out_12(ic7400_1_out_12));
  IC7400 ic7400_2 (
    .in_3(B), .in_4(ic7400_1_out_12), .in_5(ic7400_1_out_11), .in_6(ic7400_2_out_10),
    .out_10(ic7400_2_out_10), .out_11(out_4));  // open: in_1, in_2, in_7, in_8, out_9, out_12

  // Notes on the sheet:
  //   IC7400
  //   IC7400
endmodule

module IC7400 (
  input  in_1,
  input  in_2,
  input  in_3,
  input  in_4,
  input  in_5,
  input  in_6,
  input  in_7,
  input  in_8,
  output out_9,
  output out_10,
  output out_11,
  output out_12
);

  nand nand_1 (out_9, in_1, in_2);
  nand nand_2 (out_10, in_3, in_4);
  nand nand_3 (out_11, in_5, in_6);
  nand nand_4 (out_12, in_7, in_8);
endmodule
