// Logisim project Lab2 Supplementary Resource.circ as structural Verilog: 1 circuit, main circuit main
module main (
  input  in_1,
  input  in_2,
  input  in_3,
  input  in_4,
  input  in_5,
  input  in_6,
  input  in_7,
  input  in_8,
  output out_9,
  output out_10,
  output out_11,
  output out_12
);

  wire nand_1_out, nand_2_out, nand_3_out, nand_4_out, nand_6_out, nand_7_out, nand_8_out, nor_1_out,
       nor_2_out, nor_3_out, nor_4_out, nor_5_out, nor_6_out, nor_7_out;

  nand nand_1 (nand_1_out, in_1, in_2);
  nor nor_1 (nor_1_out, in_3, in_3);
  nor nor_2 (nor_2_out, in_4, in_4);
  nor nor_3 (nor_3_out, in_3, in_4);
  nand nand_2 (nand_2_out, in_5, in_6);
  nand nand_3 (nand_3_out, in_1, nand_1_out);
  nand nand_4 (nand_4_out, nand_1_out, in_2);
  nor nor_4 (nor_4_out, in_7, in_8);
  nand nand_5 (out_9, nand_3_out, nand_4_out);
  nor nor_5 (nor_5_out, nor_1_out, nor_2_out);
  nand nand_6 (nand_6_out, in_5, nand_2_out);
  nand nand_7 (nand_7_out, nand_2_out, in_6);
  nor nor_6 (nor_6_out, in_7, nor_4_out);
  nor nor_7 (nor_7_out, nor_4_out, in_8);
  nor nor_8 (out_10, nor_5_out, nor_3_out);
  nand nand_8 (nand_8_out, nand_6_out, nand_7_out);
  nor nor_9 (out_12, nor_6_out, nor_7_out);
  nand nand_9 (out_11, nand_8_out, nand_8_out);

  // Notes on the sheet:
  //   XOR Using NAND
  //   XOR Using NOR
  //   XNOR Using NAND
  //   XOR Using NOR
endmodule
