// Logisim project Task 01.circ as structural Verilog: 5 circuits, main circuit main
module main (
);

  NOT_GATE not_gate_1 ();  // open: in_1, out_2
  OR_GATE or_gate_1 ();  // open: in_1, in_2, out_3
  AND__Gate and_1 ();  // open: in_1, in_2, out_3
endmodule

module NOT_GATE (
  input  in_1,
  output out_2
);

  and and_1 (out_2, in_1, in_1);
endmodule

module AND__Gate (
  input  in_1,
  input  in_2,
  output out_3
);

  and and_1 (out_3, in_1, in_2);
endmodule

module OR_GATE (
  input  in_1,
  input  in_2,
  output out_3
);

  wire and_1_out, and_2_out;

  and and_1 (and_1_out, in_1, in_1);
  and and_2 (and_2_out, in_2, in_2);
  and and_3 (out_3, and_1_out, and_2_out);
endmodule

module NAND_GATE (
  input  in_1,
  input  in_2,
  output out_3
);

  or or_1 (out_3, in_1, in_2);
endmodule
