// Logisim project Logisim Circuit FINAL.circ as structural Verilog: 1 circuit, main circuit main
module main (
  input  in_1,
  input  in_2,
  input  in_3,
  input  in_4,
  output out_5
);

  wire and_1_out, and_2_out, not_1_out, not_2_out, not_3_out;

  not not_1 (not_1_out, in_2);
  not not_2 (not_2_out, in_1);
  not not_3 (not_3_out, in_3);
  and and_1 (and_1_out, not_1_out, not_2_out, in_4);
  and and_2 (and_2_out, not_2_out, not_3_out, in_4);
  or or_1 (out_5, and_1_out, and_2_out);

  // Notes on the sheet:
  //   A
  //   B
  //   C
  //   D
  //   B'
  //   A'
  //   A'
  //   C'
  //   A'B'D
  //   A'C'D
  //   A'B'D+A'C'D
endmodule
