// Logisim project Product SUM.circ as structural Verilog: 4 circuits, main circuit main
module main (
  input  A,
  input  B,
  input  C,
  output out_4
);

  wire n4075_1_out_10, n4075_1_out_12, n4075_2_out_10, n4075_2_out_12, n7404_1_out_7, n7404_1_out_9,
       n7404_1_out_11, n7411_1_out_9;

  _7404 u_7404_1 (
    .in_1(A), .in_3(B), .in_5(C), .out_7(n7404_1_out_7), .out_9(n7404_1_out_9), .out_11(n7404_1_out_11));  // open: in_2, in_4, in_6, out_8, out_10, out_12
  _4075 u_4075_1 (
    .in_1(n7404_1_out_9), .in_2(n7404_1_out_11), .in_3(n7404_1_out_7), .in_7(n7404_1_out_7), .in_8(B),
    .in_9(n7404_1_out_11), .out_10(n4075_1_out_10), .out_12(n4075_1_out_12));  // open: in_4, in_5, in_6, out_11
  _7411 u_7411_1 (
    .in_2(n4075_1_out_10), .out_9(n7411_1_out_9), .in_6(n4075_2_out_10), .in_7(n4075_2_out_12),
    .out_11(out_4), .in_8(n7411_1_out_9), .in_1(n4075_1_out_12));  // open: in_3, in_4, out_10, in_5
  _4075 u_4075_2 (
    .in_1(A), .in_2(B), .in_3(C), .in_7(n7404_1_out_9), .in_8(n7404_1_out_11), .in_9(A),
    .out_10(n4075_2_out_10), .out_12(n4075_2_out_12));  // open: in_4, in_5, in_6, out_11

  // Notes on the sheet:
  //   7404
  //   A'
  //   B'
  //   C'
  //   4075
  //   4075
  //   Product Of MAx Terms
  //   A+B+C
  //   A+B'+C'
  //                    A'+B'+C'
  //   A'+B+C'
  //   7411
endmodule

module _7411 (
  input  in_1,
  input  in_2,
  input  in_3,
  input  in_4,
  input  in_5,
  input  in_6,
  input  in_7,
  input  in_8,
  output out_9,
  output out_10,
  output out_11
);

  and and_1 (out_10, in_3, in_4, in_5);
  and and_2 (out_9, in_1, in_2);
  and and_3 (out_11, in_6, in_7, in_8);
endmodule

module _4075 (
  input  in_1,
  input  in_2,
  input  in_3,
  input  in_4,
  input  in_5,
  input  in_6,
  input  in_7,
  input  in_8,
  input  in_9,
  output out_10,
  output out_11,
  output out_12
);

  or or_1 (out_10, in_1, in_2, in_3);
  or or_2 (out_11, in_4, in_5, in_6);
  or or_3 (out_12, in_7, in_8, in_9);
endmodule

module _7404 (
  input  in_1,
  input  in_2,
  input  in_3,
  input  in_4,
  input  in_5,
  input  in_6,
  output out_7,
  output out_8,
  output out_9,
  output out_10,
  output out_11,
  output out_12
);

  not not_1 (out_8, in_2);
  not not_2 (out_10, in_4);
  not not_3 (out_11, in_5);
  not not_4 (out_7, in_1);
  not not_5 (out_9, in_3);
  not not_6 (out_12, in_6);
endmodule
