// Logisim project Week 01 Task 01.circ as structural Verilog: 1 circuit, main circuit main
module main (
  input  A,
  input  B,
  input  C,
  output F
);

  wire and_1_out, I2_out, I3_out, not_1_out, not_2_out, or_1_out;

  not not_1 (not_1_out, A);
  not not_2 (not_2_out, B);
  and and_1 (and_1_out, not_1_out, C);
  and I2 (I2_out, A, not_2_out);
  and I3 (I3_out, B, C);
  or or_1 (or_1_out, and_1_out, I2_out);
  or or_2 (F, or_1_out, I3_out);

  // Notes on the sheet:
  //   I 1
  //   Logic Diagram For The Given Boolean Function
  //   F=A'C+AB'+BC
  //   F=A'C+AB'+BC
endmodule
