// Logisim project Lab 04 Logisim File.circ as structural Verilog: 4 circuits, main circuit main
module main (
  input  W,
  input  X,
  input  Y,
  input  Z,
  output out_5,
  output out_6,
  output out_7,
  output out_8
);

  wire ic7404_1_out_6, ic7404_1_out_7, ic_74ls32_1_out_9, ic_74ls32_1_out_11, ic_7408_1_out_9,
       ic_7408_1_out_10, ic_7408_1_out_11, ic_7408_1_out_12, ic_7408_2_out_9, ic_7408_2_out_10,
       ic_7408_2_out_12;

  IC_7408 ic_7408_1 (
    .in_1(X), .in_2(Z), .in_3(Y), .in_4(X), .in_5(ic7404_1_out_6), .in_6(Y), .in_7(ic7404_1_out_6), .in_8(Z),
    .out_9(ic_7408_1_out_9), .out_10(ic_7408_1_out_10), .out_11(ic_7408_1_out_11), .out_12(ic_7408_1_out_12));
  IC_74LS32 ic_74ls32_1 (
    .in_1(ic_7408_1_out_10), .in_2(ic_7408_1_out_9), .in_3(W), .in_4(ic_74ls32_1_out_9),
    .in_5(ic_7408_1_out_12), .in_6(ic_7408_1_out_11), .in_7(ic_74ls32_1_out_11), .in_8(ic_7408_2_out_9),
    .out_9(ic_74ls32_1_out_9), .out_10(out_6), .out_11(ic_74ls32_1_out_11), .out_12(out_5));
  IC7404 ic7404_1 (
    .in_1(X), .in_2(Y), .in_5(Z), .out_6(ic7404_1_out_6), .out_7(ic7404_1_out_7), .out_10(out_8));  // open: in_3, in_4, out_8, out_9
  IC_7408 ic_7408_2 (
    .in_1(ic7404_1_out_7), .in_2(out_8), .in_3(out_8), .in_4(ic7404_1_out_7), .in_7(Z), .in_8(Y),
    .out_9(ic_7408_2_out_9), .out_10(ic_7408_2_out_10), .out_12(ic_7408_2_out_12));  // open: in_5, in_6, out_11
  IC_74LS32 ic_74ls32_2 (
    .in_1(ic_7408_2_out_12), .in_2(ic_7408_2_out_10), .out_9(out_7));  // open: in_3, in_4, in_5, in_6, in_7, in_8, out_10, out_11, out_12

  // Notes on the sheet:
  //   Z
  //   IC7408
  //   XY
  //   XZ
  //   w
  //   IC7404
  //   IC74LS32
  //   X'
  //   Y'
  //   Z'
  //   X'Z
  //   X'Y
  //   X'Z
  //   IC7408
  //   X'Y
  //   XY'Z'
  //   YZ
  //   Y'Z'
  //   D=Z'
  //   B=X'Z+X'Y+XY'Z'
  //   A=W+XY+XZ
  //   IC74LS32
  //   C=YZ+Y'Z'
endmodule

module IC7404 (
  input  in_1,
  input  in_2,
  input  in_3,
  input  in_4,
  input  in_5,
  output out_6,
  output out_7,
  output out_8,
  output out_9,
  output out_10
);

  not not_1 (out_6, in_1);
  not not_2 (out_7, in_2);
  not not_3 (out_8, in_3);
  not not_4 (out_9, in_4);
  not not_5 (out_10, in_5);
endmodule

module IC_7408 (
  input  in_1,
  input  in_2,
  input  in_3,
  input  in_4,
  input  in_5,
  input  in_6,
  input  in_7,
  input  in_8,
  output out_9,
  output out_10,
  output out_11,
  output out_12
);

  and and_1 (out_9, in_1, in_2);
  and and_2 (out_10, in_3, in_4);
  and and_3 (out_11, in_5, in_6);
  and and_4 (out_12, in_7, in_8);
endmodule

module IC_74LS32 (
  input  in_1,
  input  in_2,
  input  in_3,
  input  in_4,
  input  in_5,
  input  in_6,
  input  in_7,
  input  in_8,
  output out_9,
  output out_10,
  output out_11,
  output out_12
);

  or or_1 (out_9, in_1, in_2);
  or or_2 (out_10, in_3, in_4);
  or or_3 (out_11, in_5, in_6);
  or or_4 (out_12, in_7, in_8);
endmodule
