// Logisim project Lab 05 Circuit SImulator.circ as structural Verilog: 2 circuits, main circuit main
module main (
  input  M,
  input  A1,
  input  B1,
  input  A2,
  input  B2,
  input  A3,
  input  B3,
  input  A4,
  input  B4,
  output [3:0] out_10,
  output C
);

  wire adder_1_cout, adder_2_cout, adder_3_cout, n7486_1_out_9, n7486_1_out_10, n7486_1_out_11,
       n7486_1_out_12;

  _7486 u_7486_1 (
    .in_1(B4), .in_2(M), .in_3(B3), .in_4(M), .in_5(B1), .in_6(M), .in_7(B2), .in_8(M),
    .out_9(n7486_1_out_9), .out_10(n7486_1_out_10), .out_11(n7486_1_out_11), .out_12(n7486_1_out_12));
  Adder #(.width(1)) adder_1 (.a(A1), .b(n7486_1_out_11), .out(out_10[0]), .cin(M), .cout(adder_1_cout));
  Adder #(.width(1)) adder_2 (.a(A2), .b(n7486_1_out_12), .out(out_10[1]), .cin(adder_1_cout), .cout(adder_2_cout));
  Adder #(.width(1)) adder_3 (.a(A3), .b(n7486_1_out_10), .out(out_10[2]), .cin(adder_2_cout), .cout(adder_3_cout));
  Adder #(.width(1)) adder_4 (.a(A4), .b(n7486_1_out_9), .out(out_10[3]), .cin(adder_3_cout), .cout(C));
endmodule

module _7486 (
  input  in_1,
  input  in_2,
  input  in_3,
  input  in_4,
  input  in_5,
  input  in_6,
  input  in_7,
  input  in_8,
  output out_9,
  output out_10,
  output out_11,
  output out_12
);

  xor xor_1 (out_9, in_1, in_2);
  xor xor_2 (out_10, in_3, in_4);
  xor xor_3 (out_11, in_5, in_6);
  xor xor_4 (out_12, in_7, in_8);
endmodule
