// Logisim project Lab-9.circ as structural Verilog: 1 circuit, main circuit main
module main (
  input  X,
  output out_2,
  output out_3
);

  wire clock_1_out, d_ff_1_qn, xor_1_out;

  ExactlyOne xor_1 (.out(xor_1_out), .in0(out_2), .in1(X), .in2(out_3));
  Clock clock_1 (.out(clock_1_out));
  D_Flip_Flop d_ff_1 (.clk(clock_1_out), .D(d_ff_1_qn), .Q(out_3), .Qn(d_ff_1_qn));  // open: preset, en, reset
  D_Flip_Flop d_ff_2 (.clk(clock_1_out), .D(xor_1_out), .Q(out_2));  // open: Qn, preset, en, reset

  // Notes on the sheet:
  //   B
  //   A
endmodule
