// Logisim project LAB 06 Logisim FIle.circ as structural Verilog
module Task_01 (
  input  E,
  input  I0,
  input  I1,
  input  I2,
  input  I3,
  input  I4,
  input  I5,
  output out_8
);

  wire and_1_out, and_2_out, and_3_out, and_4_out, not_1_out, not_2_out;

  not not_1 (not_1_out, I4);
  not not_2 (not_2_out, I5);
  and and_1 (and_1_out, I0, not_1_out, not_2_out, E);
  and and_2 (and_2_out, I1, not_1_out, I5, E);
  and and_3 (and_3_out, I2, I4, not_2_out, E);
  and and_4 (and_4_out, I3, I4, I5, E);
  or or_1 (out_8, and_1_out, and_2_out, and_3_out, and_4_out);
endmodule

module Task_02 (
  input  in_1,
  input  in_2,
  input  in_3,
  input  in_4,
  input  in_5,
  input  in_6,
  input  in_7,
  input  in_8,
  input  [2:0] in_9,
  input  in_10,
  output out_11
);

  Multiplexer #(.select(3), .enable("false")) multiplexer_1 (
    .in0(in_1), .in1(in_2), .in2(in_3), .in3(in_4), .in4(in_5), .in5(in_6), .in6(in_7), .in7(in_8),
    .out(out_11), .sel(in_9));
endmodule
